# Fritzing sketch VaporizR2 (saved by Fritzing 0.9.3b)
circuit board: 8.46667cm x 5.64444cm

parts:
  Arduino_Nano = Arduino Nano (Rev3.0)
  Part2 = Motor Driver 1A Dual TB6612FNG
  Bluetooth = Bluetooth HC-05 Macho
  MotorA = DC Motor
  MotorB = DC Motor
  VCC2 = 4 x AAA Battery Mount
  S1 = Toggle Switch [package=THT]
  VCC3 = Battery block 9V

nets:
  N1: Arduino_Nano.D2, Bluetooth.RXD
  N2: Arduino_Nano.D3, Bluetooth.TXD
  N3: Arduino_Nano.D4, Part2.AIN1
  N4: Arduino_Nano.D5, Part2.AIN2
  N5: Arduino_Nano.D6, Part2.STBY
  N6: Arduino_Nano.D7, Part2.BIN2
  N7: Arduino_Nano.D8, Part2.BIN1
  N8: Arduino_Nano.D10, Part2.PWMB
  N9: Arduino_Nano.D11/MOSI, Part2.PWMA
  N10: Arduino_Nano.VIN, S1.L1
  GND: Arduino_Nano.GND, Part2.GND, Bluetooth.GND, VCC2.-, VCC3.-
  VCC: Arduino_Nano.5V, Part2.VCC, Bluetooth.VCC
  N11: Part2.B01, MotorB.pin_1
  N12: Part2.B02, MotorB.pin_2
  N13: Part2.A02, MotorA.pin_1
  N14: Part2.A01, MotorA.pin_2
  N15: Part2.VM, VCC2.+
  N16: S1.COM, VCC3.+
